# Fritzing sketch nfc_locker(Uno) (saved by Fritzing 0.9.5d)

parts:
  Arduino_Uno = Arduino Uno (Rev3) - ICSP
  Elechouse_PN532_NFC_RFID_Module_V3 = PN532 Elechouse RFID NFC Module V3
  220_Ohm_Resistor = Resistor [tolerance=±5% resistance=220 package="1206 [SMD]"]
  220_Ohm_Resistor_2 = Resistor [tolerance=±5% resistance=220 package="1206 [SMD]"]
  220_Ohm_Resistor_3 = Resistor [tolerance=±5% resistance=220 package="1206 [SMD]"]
  Common_Anode_RGB_LED = RGB LED (com. anode, rbg) [package="5 mm [THT]"]
  L1 = Solenoid
  Q1 = TIP120 Hi-Current Darlington Transistor
  1N4004_Diode_Rectifier = Rectifier Diode 10A
  12V_DC = 2.1mm Barrel Jack with Terminal Block

nets:
  N1: Arduino_Uno.A4/SDA, Elechouse_PN532_NFC_RFID_Module_V3.SDA
  N2: Arduino_Uno.A5/SCL, Elechouse_PN532_NFC_RFID_Module_V3.SCL
  N3: Arduino_Uno.D8, Q1.BASE
  N4: Arduino_Uno.D9_PWM, 220_Ohm_Resistor.Pin_1
  N5: Arduino_Uno.D10_PWM/SS, 220_Ohm_Resistor_2.Pin_1
  N6: Arduino_Uno.D11_PWM/MOSI, 220_Ohm_Resistor_3.Pin_1
  GND: Arduino_Uno.GND, Elechouse_PN532_NFC_RFID_Module_V3.GND, Common_Anode_RGB_LED.common_anode, Q1.EMITTER, 1N4004_Diode_Rectifier.anode, 12V_DC.NEG
  5V: Arduino_Uno.5V, Elechouse_PN532_NFC_RFID_Module_V3.VCC
  N7: 220_Ohm_Resistor.Pin_0, Common_Anode_RGB_LED.red_cathode
  N8: 220_Ohm_Resistor_2.Pin_0, Common_Anode_RGB_LED.green_cathode
  N9: 220_Ohm_Resistor_3.Pin_0, Common_Anode_RGB_LED.blue_cathode
  N10: L1.pin1, Q1.COLLECTOR, 1N4004_Diode_Rectifier.cathode
  N11: L1.pin2, 12V_DC.POS

notes:
  The PN532 module needs its DIP switches set for I2C
  Channel 1 = On
  Channel 2 = Off

custom parts:
  PN532 Elechouse RFID NFC Module V3: NFC is a popular technology in recent years. We often heard this work while smart phone company such as Samsung or HTC introduces their latest high-end phones. Almost all the high-end phone in the market support NFC. Near field communication (NFC) is a set of standards for smart phones and similar devices to establish radio communication with each other by touching them together or bringing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
