# Fritzing sketch nfc_tag_batch_writer(Uno) (saved by Fritzing 0.9.5d)
breadboards: 1

parts:
  Arduino_Uno = Arduino Uno (Rev3) - ICSP
  Elechouse_PN532_NFC_RFID_Module_V3 = PN532 Elechouse RFID NFC Module V3
  Adafruit_0_56"_7-segment_LED_HT16K33_Backpack = 0.56" 7-segment LED Backpack [part_number=878]
  microSD1 = MicroSD Card Module

nets:
  N1: Arduino_Uno.A4/SDA, Elechouse_PN532_NFC_RFID_Module_V3.SDA, Adafruit_0_56"_7-segment_LED_HT16K33_Backpack.SDA
  N2: Arduino_Uno.A5/SCL, Elechouse_PN532_NFC_RFID_Module_V3.SCL, Adafruit_0_56"_7-segment_LED_HT16K33_Backpack.SCL
  N3: Arduino_Uno.ICSP_MISO, Arduino_Uno.D12/MISO, microSD1.MISO
  N4: Arduino_Uno.D11_PWM/MOSI, microSD1.MOSI
  N5: Arduino_Uno.D13/SCK, microSD1.SCK
  N6: Arduino_Uno.D4, microSD1.CS
  VCC: Arduino_Uno.5V, Elechouse_PN532_NFC_RFID_Module_V3.VCC, Adafruit_0_56"_7-segment_LED_HT16K33_Backpack.VDD, microSD1.VCC
  GND: Arduino_Uno.GND, Elechouse_PN532_NFC_RFID_Module_V3.GND, Adafruit_0_56"_7-segment_LED_HT16K33_Backpack.GND, microSD1.GND

notes:
  The PN532 module needs its DIP switches set for I2C
  Channel 1 = On
  Channel 2 = Off

custom parts:
  PN532 Elechouse RFID NFC Module V3: NFC is a popular technology in recent years. We often heard this work while smart phone company such as Samsung or HTC introduces their latest high-end phones. Almost all the high-end phone in the market support NFC. Near field communication (NFC) is a set of standards for smart phones and similar devices to establish radio communication with each other by touching them together or bringing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
  0.56" 7-segment LED Backpack: This 0.56" 7-segment LED display includes a driver chip for simple control via an I2C interface. The backpack features address-selection jumpers so you can connect up to eight displays on a single I2C bus.
